# Fritzing sketch calc (saved by Fritzing 0.8.7b)
breadboards: 1

parts:
  Raspberry_Pi_B_rev1 = Raspberry Pi B rev2
  LED1 = LED - 5mm [color="Red (633nm)" package="5 mm [THT]"]
  LED2 = LED - 5mm [color="Red (633nm)" package="5 mm [THT]"]
  LED3 = LED - 5mm [color="Red (633nm)" package="5 mm [THT]"]
  LED4 = LED - 5mm [color="Red (633nm)" package="5 mm [THT]"]
  LED5 = LED - 5mm [color="Red (633nm)" package="5 mm [THT]"]
  LED6 = LED - 5mm [color="Red (633nm)" package="5 mm [THT]"]
  LED7 = LED - 5mm [color="Red (633nm)" package="5 mm [THT]"]
  LED8 = LED - 5mm [color="Red (633nm)" package="5 mm [THT]"]

nets:
  N1: Raspberry_Pi_B_rev1.3V3, Raspberry_Pi_B_rev1.GPIO_24, LED3.anode
  N2: Raspberry_Pi_B_rev1.GPIO_3, Raspberry_Pi_B_rev1.GND, Raspberry_Pi_B_rev1.GPIO_23, Raspberry_Pi_B_rev1.GPIO_17, Raspberry_Pi_B_rev1.GPIO_18, Raspberry_Pi_B_rev1.GPIO_22, LED1.cathode, LED2.cathode, LED3.cathode, LED4.cathode, LED5.cathode, LED6.cathode, LED7.cathode, LED7.anode, LED8.cathode
  N3: Raspberry_Pi_B_rev1.GPIO_15, Raspberry_Pi_B_rev1.GPIO_4, LED8.anode
  N4: Raspberry_Pi_B_rev1.GPIO_27, LED6.anode
  N5: Raspberry_Pi_B_rev1.GPIO_9, Raspberry_Pi_B_rev1.GPIO_25, LED4.anode
